// Logisim project 150120031_150121545_150120995.circ as structural Verilog: 15 circuits, main circuit ALU
module ALU (
  input  Control,
  input  [17:0] Input_1,
  input  [17:0] Input_2,
  input  [5:0] Imm,
  input  Carry_In,
  input  [17:0] Unused_Input,
  input  [2:0] Which_Operation,
  output C_Out,
  output [17:0] Output,
  output C_Out_2
);

  wire [17:0] ADD_output, ADDI_output, AND_out, ANDI_out, NAND_out, NOR_out, SignExt__6_to_18_out_2;

  SignExt_6_to18 SignExt__6_to_18 (.in_1(Imm), .out_2(SignExt__6_to_18_out_2));
  _18_Bit_FullAdder ADD (.Input_1(Input_1), .Input_2(Input_2), .C_In(Carry_In), .Output(ADD_output), .C_Out(C_Out));
  assign AND_out = Input_1 & Input_2;  // AND_Gate AND, 18 bits wide
  assign NAND_out = ~(Input_1 & Input_2);  // NAND_Gate NAND, 18 bits wide
  assign NOR_out = ~(Input_2 | Input_1);  // NOR_Gate NOR, 18 bits wide
  _18_Bit_FullAdder ADDI (
    .Input_1(Input_1), .Input_2(SignExt__6_to_18_out_2), .C_In(Carry_In), .Output(ADDI_output),
    .C_Out(C_Out_2));
  assign ANDI_out = Input_1 & SignExt__6_to_18_out_2;  // AND_Gate ANDI, 18 bits wide
  Multiplexer #(.select(3), .width(18)) multiplexer_1 (
    .in0(ADD_output), .in1(AND_out), .in2(NAND_out), .in3(NOR_out), .in4(ADDI_output), .in5(ANDI_out),
    .in6(Unused_Input), .in7(Unused_Input), .out(Output), .sel(Which_Operation), .en(Control));
endmodule

module Register_File (
  input  [17:0] data,
  input  [3:0] Reg_DEST,
  input  [3:0] Reg_1,
  input  [3:0] Reg_2,
  input  regWrite,
  output [17:0] Reg_1_Data,
  output [17:0] Reg_2_Data
);

  wire and_1_out, and_2_out, and_3_out, and_4_out, and_5_out, and_6_out, and_7_out, and_8_out, and_9_out,
       and_10_out, and_11_out, and_12_out, and_13_out, and_14_out, and_15_out, and_16_out, clock_1_out,
       decoder_1_out0, decoder_1_out1, decoder_1_out2, decoder_1_out3, decoder_1_out4, decoder_1_out5,
       decoder_1_out6, decoder_1_out7, decoder_1_out8, decoder_1_out9, decoder_1_out10, decoder_1_out11,
       decoder_1_out12, decoder_1_out13, decoder_1_out14, decoder_1_out15;
  wire [17:0] n18_bit_register_1_output, n18_bit_register_2_output, n18_bit_register_3_output,
       n18_bit_register_4_output, n18_bit_register_5_output, n18_bit_register_6_output,
       n18_bit_register_7_output, n18_bit_register_8_output, n18_bit_register_9_output,
       n18_bit_register_10_output, n18_bit_register_11_output, n18_bit_register_12_output,
       n18_bit_register_13_output, n18_bit_register_14_output, n18_bit_register_15_output,
       n18_bit_register_16_output;

  Decoder #(.select(4)) decoder_1 (
    .out0(decoder_1_out0), .out1(decoder_1_out1), .out2(decoder_1_out2), .out3(decoder_1_out3),
    .out4(decoder_1_out4), .out5(decoder_1_out5), .out6(decoder_1_out6), .out7(decoder_1_out7),
    .out8(decoder_1_out8), .out9(decoder_1_out9), .out10(decoder_1_out10), .out11(decoder_1_out11),
    .out12(decoder_1_out12), .out13(decoder_1_out13), .out14(decoder_1_out14), .out15(decoder_1_out15),
    .sel(Reg_DEST));  // open: en
  and and_1 (and_1_out, decoder_1_out0, regWrite);
  and and_2 (and_2_out, decoder_1_out1, regWrite);
  and and_3 (and_3_out, decoder_1_out2, regWrite);
  and and_4 (and_4_out, decoder_1_out3, regWrite);
  and and_5 (and_5_out, decoder_1_out4, regWrite);
  and and_6 (and_6_out, decoder_1_out5, regWrite);
  and and_7 (and_7_out, decoder_1_out6, regWrite);
  and and_8 (and_8_out, decoder_1_out7, regWrite);
  Clock clock_1 (.out(clock_1_out));
  _18_Bit_Register u_18_bit_register_1 (
    .Data(data), .Write_Enabled(and_1_out), .Clear(1'b0), .Clock(clock_1_out),
    .Output(n18_bit_register_1_output));
  _18_Bit_Register u_18_bit_register_2 (
    .Data(data), .Write_Enabled(and_2_out), .Clear(1'b0), .Clock(clock_1_out),
    .Output(n18_bit_register_2_output));
  _18_Bit_Register u_18_bit_register_3 (
    .Data(data), .Write_Enabled(and_3_out), .Clear(1'b0), .Clock(clock_1_out),
    .Output(n18_bit_register_3_output));
  _18_Bit_Register u_18_bit_register_4 (
    .Data(data), .Write_Enabled(and_4_out), .Clear(1'b0), .Clock(clock_1_out),
    .Output(n18_bit_register_4_output));
  _18_Bit_Register u_18_bit_register_5 (
    .Data(data), .Write_Enabled(and_5_out), .Clear(1'b0), .Clock(clock_1_out),
    .Output(n18_bit_register_5_output));
  _18_Bit_Register u_18_bit_register_6 (
    .Data(data), .Write_Enabled(and_6_out), .Clear(1'b0), .Clock(clock_1_out),
    .Output(n18_bit_register_6_output));
  _18_Bit_Register u_18_bit_register_7 (
    .Data(data), .Write_Enabled(and_7_out), .Clear(1'b0), .Clock(clock_1_out),
    .Output(n18_bit_register_7_output));
  _18_Bit_Register u_18_bit_register_8 (
    .Data(data), .Write_Enabled(and_8_out), .Clear(1'b0), .Clock(clock_1_out),
    .Output(n18_bit_register_8_output));
  and and_9 (and_9_out, decoder_1_out8, regWrite);
  and and_10 (and_10_out, decoder_1_out9, regWrite);
  and and_11 (and_11_out, decoder_1_out10, regWrite);
  and and_12 (and_12_out, decoder_1_out11, regWrite);
  and and_13 (and_13_out, decoder_1_out12, regWrite);
  and and_14 (and_14_out, decoder_1_out13, regWrite);
  and and_15 (and_15_out, decoder_1_out14, regWrite);
  and and_16 (and_16_out, decoder_1_out15, regWrite);
  _18_Bit_Register u_18_bit_register_9 (
    .Data(data), .Write_Enabled(and_9_out), .Clear(1'b0), .Clock(clock_1_out),
    .Output(n18_bit_register_9_output));
  _18_Bit_Register u_18_bit_register_10 (
    .Data(data), .Write_Enabled(and_10_out), .Clear(1'b0), .Clock(clock_1_out),
    .Output(n18_bit_register_10_output));
  _18_Bit_Register u_18_bit_register_11 (
    .Data(data), .Write_Enabled(and_11_out), .Clear(1'b0), .Clock(clock_1_out),
    .Output(n18_bit_register_11_output));
  _18_Bit_Register u_18_bit_register_12 (
    .Data(data), .Write_Enabled(and_12_out), .Clear(1'b0), .Clock(clock_1_out),
    .Output(n18_bit_register_12_output));
  _18_Bit_Register u_18_bit_register_13 (
    .Data(data), .Write_Enabled(and_13_out), .Clear(1'b0), .Clock(clock_1_out),
    .Output(n18_bit_register_13_output));
  _18_Bit_Register u_18_bit_register_14 (
    .Data(data), .Write_Enabled(and_14_out), .Clear(1'b0), .Clock(clock_1_out),
    .Output(n18_bit_register_14_output));
  _18_Bit_Register u_18_bit_register_15 (
    .Data(data), .Write_Enabled(and_15_out), .Clear(1'b0), .Clock(clock_1_out),
    .Output(n18_bit_register_15_output));
  _18_Bit_Register u_18_bit_register_16 (
    .Data(data), .Write_Enabled(and_16_out), .Clear(1'b0), .Clock(clock_1_out),
    .Output(n18_bit_register_16_output));
  Multiplexer #(.select(4), .width(18)) multiplexer_1 (
    .in0(n18_bit_register_9_output), .in1(n18_bit_register_1_output), .in2(n18_bit_register_10_output),
    .in3(n18_bit_register_2_output), .in4(n18_bit_register_11_output), .in5(n18_bit_register_3_output),
    .in6(n18_bit_register_12_output), .in7(n18_bit_register_4_output), .in8(n18_bit_register_8_output),
    .in9(n18_bit_register_16_output), .in10(n18_bit_register_7_output), .in11(n18_bit_register_15_output),
    .in12(n18_bit_register_6_output), .in13(n18_bit_register_14_output), .in14(n18_bit_register_5_output),
    .in15(n18_bit_register_13_output), .out(Reg_1_Data), .sel(Reg_1));  // open: en
  Multiplexer #(.select(4), .width(18)) multiplexer_2 (
    .in0(n18_bit_register_4_output), .in1(n18_bit_register_12_output), .in2(n18_bit_register_3_output),
    .in3(n18_bit_register_11_output), .in4(n18_bit_register_2_output), .in5(n18_bit_register_10_output),
    .in6(n18_bit_register_1_output), .in7(n18_bit_register_9_output), .in8(n18_bit_register_13_output),
    .in9(n18_bit_register_5_output), .in10(n18_bit_register_14_output), .in11(n18_bit_register_6_output),
    .in12(n18_bit_register_15_output), .in13(n18_bit_register_7_output), .in14(n18_bit_register_16_output),
    .in15(n18_bit_register_8_output), .out(Reg_2_Data), .sel(Reg_2));  // open: en
endmodule

module HalfAdder (
  input  Input_1,
  input  Input_2,
  output Sum,
  output C_out
);

  xor xor_1 (Sum, Input_1, Input_2);
  and and_1 (C_out, Input_1, Input_2);
endmodule

module FullAdder (
  input  Input_1,
  input  Input_2,
  input  C_In,
  output Sum,
  output C_out
);

  wire and_1_out, and_2_out, xor_1_out;

  xor xor_1 (xor_1_out, Input_1, Input_2);
  and and_1 (and_1_out, Input_1, Input_2);
  and and_2 (and_2_out, xor_1_out, C_In);
  xor xor_2 (Sum, xor_1_out, C_In);
  or or_1 (C_out, and_2_out, and_1_out);
endmodule

module _8_Bit_FullAdder (
  input  [7:0] Input_1,
  input  [7:0] Input_2,
  input  C_In,
  output [7:0] Output,
  output C_Out
);

  wire fulladder_1_c_out, fulladder_2_c_out, fulladder_3_c_out, fulladder_4_c_out, fulladder_5_c_out,
       fulladder_6_c_out, fulladder_7_c_out;

  FullAdder fulladder_1 (
    .Input_1(Input_1[0]), .Input_2(Input_2[0]), .C_In(C_In), .Sum(Output[0]), .C_out(fulladder_1_c_out));
  FullAdder fulladder_2 (
    .Input_1(Input_1[1]), .Input_2(Input_2[1]), .C_In(fulladder_1_c_out), .Sum(Output[1]),
    .C_out(fulladder_2_c_out));
  FullAdder fulladder_3 (
    .Input_1(Input_1[2]), .Input_2(Input_2[2]), .C_In(fulladder_2_c_out), .Sum(Output[2]),
    .C_out(fulladder_3_c_out));
  FullAdder fulladder_4 (
    .Input_1(Input_1[3]), .Input_2(Input_2[3]), .C_In(fulladder_3_c_out), .Sum(Output[3]),
    .C_out(fulladder_4_c_out));
  FullAdder fulladder_5 (
    .Input_1(Input_1[4]), .Input_2(Input_2[4]), .C_In(fulladder_4_c_out), .Sum(Output[4]),
    .C_out(fulladder_5_c_out));
  FullAdder fulladder_6 (
    .Input_1(Input_1[5]), .Input_2(Input_2[5]), .C_In(fulladder_5_c_out), .Sum(Output[5]),
    .C_out(fulladder_6_c_out));
  FullAdder fulladder_7 (
    .Input_1(Input_1[6]), .Input_2(Input_2[6]), .C_In(fulladder_6_c_out), .Sum(Output[6]),
    .C_out(fulladder_7_c_out));
  FullAdder fulladder_8 (
    .Input_1(Input_1[7]), .Input_2(Input_2[7]), .C_In(fulladder_7_c_out), .Sum(Output[7]), .C_out(C_Out));
endmodule

module _18_Bit_FullAdder (
  input  [17:0] Input_1,
  input  [17:0] Input_2,
  input  C_In,
  output [17:0] Output,
  output C_Out
);

  wire _8_Bit_FullAdder_2_c_out, _8_Bit_FullAdder_c_out, FullAdder_c_out;

  _8_Bit_FullAdder _8_Bit_FullAdder (
    .Input_1(Input_1[7:0]), .Input_2(Input_2[7:0]), .C_In(C_In), .Output(Output[7:0]),
    .C_Out(_8_Bit_FullAdder_c_out));
  _8_Bit_FullAdder _8_Bit_FullAdder_2 (
    .Input_1(Input_1[15:8]), .Input_2(Input_2[15:8]), .C_In(_8_Bit_FullAdder_c_out), .Output(Output[15:8]),
    .C_Out(_8_Bit_FullAdder_2_c_out));
  FullAdder FullAdder (
    .Input_1(Input_1[16]), .Input_2(Input_2[16]), .C_In(_8_Bit_FullAdder_2_c_out), .Sum(Output[16]),
    .C_out(FullAdder_c_out));
  FullAdder FullAdder_2 (
    .Input_1(Input_1[17]), .Input_2(Input_2[17]), .C_In(FullAdder_c_out), .Sum(Output[17]), .C_out(C_Out));
endmodule

module _1_Bit_Register (
  input  Data,
  input  Write_Enabled,
  input  Clear,
  input  Clock,
  output Output
);

  wire and_1_out, and_2_out, not_1_out, or_1_out;

  not not_1 (not_1_out, Write_Enabled);
  and and_1 (and_1_out, Data, Write_Enabled);
  and and_2 (and_2_out, not_1_out, Output);
  or or_1 (or_1_out, and_1_out, and_2_out);
  D_Flip_Flop d_ff_1 (.clk(Clock), .D(or_1_out), .Q(Output), .reset(Clear));  // open: Qn, preset, en
endmodule

module _4_Bit_Register (
  input  [3:0] Data,
  input  Write_Enabled,
  input  Clear,
  input  Clock,
  output [3:0] Output
);

  _1_Bit_Register u_1_bit_register_1 (
    .Data(Data[0]), .Write_Enabled(Write_Enabled), .Clear(Clear), .Clock(Clock), .Output(Output[0]));
  _1_Bit_Register u_1_bit_register_2 (
    .Data(Data[1]), .Write_Enabled(Write_Enabled), .Clear(Clear), .Clock(Clock), .Output(Output[1]));
  _1_Bit_Register u_1_bit_register_3 (
    .Data(Data[2]), .Write_Enabled(Write_Enabled), .Clear(Clear), .Clock(Clock), .Output(Output[2]));
  _1_Bit_Register u_1_bit_register_4 (
    .Data(Data[3]), .Write_Enabled(Write_Enabled), .Clear(Clear), .Clock(Clock), .Output(Output[3]));
endmodule

module SignExt_4_to18 (
  input  [3:0] in_1,
  output [17:0] out_2
);


  assign out_2 = {{15{in_1[3]}}, in_1[2:0]};
endmodule

module SignExt_6_to18 (
  input  [5:0] in_1,
  output [17:0] out_2
);


  assign out_2 = {{13{in_1[5]}}, in_1[4:0]};
endmodule

module SignExt_10_to18 (
  input  [9:0] in_1,
  output [17:0] out_2
);


  assign out_2 = {{9{in_1[9]}}, in_1[8:0]};
endmodule

module PC (
  input  write,
  input  [17:0] \input ,
  input  en,
  input  clk,
  output [17:0] \output 
);

  wire [17:0] multiplexer_1_out;

  Multiplexer #(.width(18), .enable("false")) multiplexer_1 (
    .in0(\output ), .in1(\input ), .out(multiplexer_1_out), .sel(write));
  Register #(.width(18)) register_1 (.D(multiplexer_1_out), .en(en), .Q(\output ), .clk(clk), .clr(1'b0));
endmodule

module _18_Bit_Register (
  input  [17:0] Data,
  input  Write_Enabled,
  input  Clear,
  input  Clock,
  output [17:0] Output
);

  _4_Bit_Register u_4_bit_register_1 (
    .Data(Data[3:0]), .Write_Enabled(Write_Enabled), .Clear(Clear), .Clock(Clock), .Output(Output[3:0]));
  _4_Bit_Register u_4_bit_register_2 (
    .Data(Data[7:4]), .Write_Enabled(Write_Enabled), .Clear(Clear), .Clock(Clock), .Output(Output[7:4]));
  _4_Bit_Register u_4_bit_register_3 (
    .Data(Data[11:8]), .Write_Enabled(Write_Enabled), .Clear(Clear), .Clock(Clock), .Output(Output[11:8]));
  _4_Bit_Register u_4_bit_register_4 (
    .Data(Data[15:12]), .Write_Enabled(Write_Enabled), .Clear(Clear), .Clock(Clock), .Output(Output[15:12]));
  _1_Bit_Register u_1_bit_register_1 (
    .Data(Data[16]), .Write_Enabled(Write_Enabled), .Clear(Clear), .Clock(Clock), .Output(Output[16]));
  _1_Bit_Register u_1_bit_register_2 (
    .Data(Data[17]), .Write_Enabled(Write_Enabled), .Clear(Clear), .Clock(Clear), .Output(Output[17]));
endmodule

module Control_Unit (
  input  [17:0] in_1,
  input  in_2,
  output out_3,
  output Mux1,
  output out_5,
  output out_6,
  output out_7,
  output Memory_Write,
  output out_9,
  output out_10,
  output InstrRead,
  output PCread
);

  wire clock_1_out, decoder_1_out0, decoder_1_out1, decoder_1_out2, decoder_1_out3, decoder_1_out4,
       decoder_1_out5, decoder_1_out6, decoder_1_out8, decoder_1_out9, decoder_1_out10, decoder_1_out11,
       decoder_1_out12, decoder_1_out13, decoder_1_out14, decoder_1_out15;
  wire [3:0] n4_bit_register_1_output;

  Clock clock_1 (.out(clock_1_out));
  _4_Bit_Register u_4_bit_register_1 (
    .Data(in_1[17:14]), .Clear(in_2), .Clock(clock_1_out), .Output(n4_bit_register_1_output));  // open: Write_Enabled
  Decoder #(.select(4), .enable("false")) decoder_1 (
    .out0(decoder_1_out0), .out1(decoder_1_out1), .out2(decoder_1_out2), .out3(decoder_1_out3),
    .out4(decoder_1_out4), .out5(decoder_1_out5), .out6(decoder_1_out6), .out7(Memory_Write),
    .out8(decoder_1_out8), .out9(decoder_1_out9), .out10(decoder_1_out10), .out11(decoder_1_out11),
    .out12(decoder_1_out12), .out13(decoder_1_out13), .out14(decoder_1_out14), .out15(decoder_1_out15),
    .sel(n4_bit_register_1_output));
  or or_1 (out_9, decoder_1_out10, decoder_1_out12, decoder_1_out11);
  or or_2 (out_10, decoder_1_out13, decoder_1_out14);
  or PC_Write (out_3, decoder_1_out0, decoder_1_out1, decoder_1_out2, decoder_1_out3, decoder_1_out4, decoder_1_out5, decoder_1_out6, Memory_Write, decoder_1_out8);
  or ALU (out_5, decoder_1_out0, decoder_1_out1, decoder_1_out2, decoder_1_out15, decoder_1_out3, decoder_1_out4, decoder_1_out5);
  not not_1 (out_6, decoder_1_out9);
  or Memory_Read (out_7, decoder_1_out6, decoder_1_out8);

  assign InstrRead = 1'b1;
  assign Mux1 = in_1[0];
  assign PCread = 1'b1;

  // Notes on the sheet:
  //   ADD
  //   AND
  //   NAND
  //   NOR
  //   ADDI
  //   ANDI
  //   LD
  //   ST
  //   CMP
  //   JUMP
  //   JE
  //   JA
  //   JB
  //   JAE
  //   JBE
  //   ALU
endmodule

module main (
);

  wire adder_1_cout, alu_1_c_out, clock_1_out, control_unit_1_memory_write, control_unit_1_out_3,
       control_unit_1_out_5, control_unit_1_out_6, control_unit_1_out_7, control_unit_1_out_9,
       control_unit_1_pcread, n18_bit_register_1_p3;
  wire [5:0] undriven;
  wire [17:0] adder_1_out, alu_1_output, multiplexer_1_out, multiplexer_2_out, multiplexer_4_out,
       multiplexer_5_out, multiplexer_7_out, n18_bit_register_1_p1, n18_bit_register_1_p2,
       n18_bit_register_1_p4, n18_bit_register_1_p5, n18_bit_register_2_output, pc_1_output, ram_1_data,
       rom_1_data, undriven_2, undriven_3, undriven_4;

  PC pc_1 (
    .\input (multiplexer_7_out), .write(n18_bit_register_1_p3), .en(control_unit_1_pcread),
    .clk(clock_1_out), .\output (pc_1_output));
  PC pc_2 (
    .\input (multiplexer_7_out), .write(n18_bit_register_1_p3), .en(control_unit_1_pcread),
    .clk(clock_1_out), .\output (pc_1_output));
  Clock clock_1 (.out(clock_1_out));
  ROM #(.addrWidth(18), .dataWidth(18)) rom_1 (.addr(pc_1_output), .data(rom_1_data), .sel(1'b1));
  Adder #(.width(18)) adder_1 (.a(pc_1_output), .b(18'h1), .out(adder_1_out), .cin(1'b0), .cout(adder_1_cout));
  // _18_Bit_Register 18_bit_register_1: pin names not known; wires that end beside it: n18_bit_register_1_p1, n18_bit_register_1_p2, n18_bit_register_1_p3, n18_bit_register_1_p4, n18_bit_register_1_p5
  _18_Bit_Register u_18_bit_register_2 (
    .Data(rom_1_data), .Output(n18_bit_register_2_output));  // open: Write_Enabled, Clear, Clock
  Control_Unit control_unit_1 (
    .in_2(clock_1_out), .out_3(control_unit_1_out_3), .Mux1(control_unit_1_out_3),
    .out_5(control_unit_1_out_5), .out_6(control_unit_1_out_6), .out_7(control_unit_1_out_7),
    .Memory_Write(control_unit_1_memory_write), .out_9(control_unit_1_out_9),
    .InstrRead(n18_bit_register_1_p3), .PCread(control_unit_1_pcread));  // open: in_1, out_10
  ALU alu_1 (
    .Input_1(n18_bit_register_1_p5), .Input_2(n18_bit_register_1_p5), .Imm(undriven),
    .Unused_Input(multiplexer_2_out), .C_Out(alu_1_c_out), .Output(alu_1_output));  // open: Carry_In, Which_Operation, Control, C_Out_2
  Multiplexer #(.width(18), .enable("false")) multiplexer_1 (
    .in0(alu_1_output), .in1(undriven_2), .out(multiplexer_1_out), .sel(control_unit_1_out_5));
  Multiplexer #(.width(18), .enable("false")) multiplexer_2 (
    .in0(n18_bit_register_1_p4), .in1(n18_bit_register_2_output), .out(multiplexer_2_out),
    .sel(control_unit_1_memory_write));
  Multiplexer #(.width(18), .enable("false")) multiplexer_3 (
    .in0(undriven_3), .in1(undriven_4), .out(n18_bit_register_1_p1), .sel(control_unit_1_out_7));
  Adder #(.width(18)) adder_2 (.a(undriven_2), .b(adder_1_out), .cin(1'b0));  // open: out, cout
  Multiplexer #(.width(18), .enable("false")) multiplexer_4 (
    .in0(undriven_3), .in1(undriven_4), .out(multiplexer_4_out), .sel(control_unit_1_out_3));
  RAM #(.addrWidth(18), .dataWidth(18), .bus("separate")) ram_1 (
    .addr(multiplexer_1_out), .data(ram_1_data), .sel(1'b1), .clk(clock_1_out), .clr(1'b0));  // open: din, str, ld
  Multiplexer #(.width(18), .enable("false")) multiplexer_5 (
    .in0(ram_1_data), .in1(multiplexer_1_out), .out(multiplexer_5_out), .sel(control_unit_1_out_3));
  Multiplexer #(.width(18), .enable("false")) multiplexer_6 (
    .in0(multiplexer_5_out), .in1(n18_bit_register_1_p2), .out(n18_bit_register_1_p5),
    .sel(control_unit_1_out_9));
  Multiplexer #(.width(18), .enable("false")) multiplexer_7 (
    .in0(multiplexer_5_out), .in1(n18_bit_register_1_p2), .out(multiplexer_7_out), .sel(control_unit_1_out_6));
endmodule
